// Digital circuit SUBLEQ24.dig as structural Verilog
module SUBLEQ24 (
  input  XTAL,
  input  TraceClock,
  input  TRACE,
  input  clk,
  input  BAUDCLK
);

  wire _74ls125_1_y4, _74ls175_1_q1, _74ls175_1_q2, _74ls175_1_q3, _74ls175_1_q4, _74ls175_2_nq1,
       _74ls175_2_nq2, _74ls175_2_nq3, _74ls175_2_nq4, _74ls540_1_n6o, _74ls540_1_n7o, _74ls541_1__6o,
       _74ls541_1__7o, _74ls4017_1_q7, A_CK, AisNeg, and_1_out, and_2_out, and_3_out, and_4_out, and_5_out,
       and_6_out, and_7_out, and_8_out, and_9_out, and_10_out, and_11_out, Aval_CK, B_CK, BisNeg, Bval_CK,
       d_ff_1_q, d_ff_2_q, delay_1_out, half7474_1_nq, half7474_1_q, half7474_2_q, half7474_3_q,
       half7474_4_nq, half7474_5_q, INTREQ, IOread, IOwrite, isLEQ, M_out, MAR_CK, MopEnd, nand_1_out,
       nand_2_out, nand_3_out, nBusRq, nCK, nIOread, nIOreadP, nIOwrite, nIOwriteP, nMAR_E, nor_2_out,
       not_2_out, not_4_out, not_6_out, not_9_out, not_10_out, not_11_out, not_12_out, not_14_out, nPC_E,
       nPC_LD, nRD, nReset, nResetP, nResult_E, nUARTavailRead, nUARTbusyRead, nUARTrxdRead, nWR, or_1_out,
       or_2_out, or_3_out, or_4_out, or_5_out, or_6_out, or_8_out, or_9_out, or_11_out, or_12_out, or_13_out,
       or_14_out, PC_CK, PC_FLASH, PCbit0, PCneg, POR, pullup_1_out, pullup_3_out, R_out, RUN, S_out,
       seqPCck, Tick, TS0, TS1, TS2, TS3, TS4, TS5, UARTtxdWrite, undriven, undriven_2, Z_out;
  wire [7:0] _74ls574_1_spy, _74ls574_2_spy, _74ls574_3_spy, subleq24_gpio_1_port2out;
  wire [19:0] barrelshifter_1_out, counter_1_out, d_ff_4_q;
  wire [23:0] ABUS, d_ff_5_q, DBUS, not_7_out, not_8_out, ramasync_1_q, SPY_aval, SPY_bval, SPY_PC, SPY_sub;

  Button R (.out(R_out));
  Button S (.out(S_out));
  and and_1 (and_1_out, PCneg, PCbit0);
  and and_2 (and_2_out, TRACE, TraceClock);
  Button F (.out(PC_FLASH));
  Button Z (.out(Z_out));
  // Probe on and_1_out
  or or_1 (or_1_out, R_out, S_out, and_2_out);
  or or_2 (or_2_out, PC_FLASH, Z_out, Z_out);
  not not_1 (nReset, or_2_out);
  _74LS175 _74ls175_1 (
    .D1(or_2_out), .D2(and_1_out), .D3(R_out), .D4(or_1_out), .CLK(XTAL), .nCL(nResetP), .Q1(_74ls175_1_q1),
    .Q2(_74ls175_1_q2), .Q3(_74ls175_1_q3), .Q4(_74ls175_1_q4));  // open: nQ1, nQ2, nQ3, nQ4
  or or_3 (or_3_out, nWR, POR);
  SUBLEQ24_PC subleq24_pc_1 (
    .DBUS(DBUS), .nResetP(nResetP), .PC_CK(PC_CK), .nPC_LD(nPC_LD), .nE_PC(nPC_E), .PC_FLASH(PC_FLASH),
    .ABUS(ABUS), .PC_neg(PCneg), .SPY_PC(SPY_PC), .PCbit0(PCbit0));
  SUBLEQ24_MAR subleq24_mar_1 (
    .DBUS(DBUS), .MAR_CK(MAR_CK), .nMAR_E(nMAR_E), .nRESET(nReset), .TS0(TS0), .B_CK(B_CK), .A_CK(A_CK),
    .ABUS(ABUS), .AisNeg(AisNeg), .BisNeg(BisNeg));
  SUBLEQ24_SUBTRACTOR subleq24_subtractor_1 (
    .DBUS(DBUS), .nIOwrite(nIOwrite), .nResult_E(nResult_E), .Aval_CK(Aval_CK), .Bval_CK(Bval_CK),
    .DBUSo(DBUS), .isLEQ(isLEQ), .SPY_sub(SPY_sub));
  SUBLEQ24_GPIO subleq24_gpio_1 (
    .DBUS(DBUS), .GPIO2in(8'h2a), .nIOwriteP(nIOwriteP), .nIOreadP(nIOreadP), .A_ck(A_CK), .B_ck(B_CK),
    .DBUSo(DBUS), .nUARTrxdRead(nUARTrxdRead), .nUARTavailRead(nUARTavailRead),
    .nUARTbusyRead(nUARTbusyRead), .UARTtxdWrite(UARTtxdWrite), .PORT2OUT(subleq24_gpio_1_port2out));
  SUBLEQ24_SERIAL subleq24_serial_1 (
    .DBUS(DBUS), .nReset(nReset), .UARTtxdWrite(UARTtxdWrite), .nUARTbusyRead(nUARTbusyRead),
    .nUARTavailRead(nUARTavailRead), .nUARTrxdRead(nUARTrxdRead), .BAUDCLK(BAUDCLK), .DBUS0(DBUS));
  RAMAsync #(.AddrBits(24), .isProgramMemory("true"), .Bits(24)) ramasync_1 (
    .A(ABUS), .D(DBUS), .we(~or_3_out), .Q(ramasync_1_q));
  or or_4 (or_4_out, ~or_3_out, nRD);  // Or
  _74LS175 _74ls175_2 (
    .D1(_74ls175_1_q1), .D2(_74ls175_1_q2), .D3(_74ls175_1_q3), .D4(_74ls175_1_q4), .CLK(XTAL),
    .nCL(nResetP), .nQ1(_74ls175_2_nq1), .nQ2(_74ls175_2_nq2), .nQ3(_74ls175_2_nq3), .nQ4(_74ls175_2_nq4));  // open: Q1, Q2, Q3, Q4
  D_FF d_ff_1 (.D(1'b1), .C(TraceClock), .Q(d_ff_1_q));  // open: nQ
  assign DBUS = ~or_4_out ? ramasync_1_q : 24'bz;  // DriverInvSel driverinvsel_1
  D_FF d_ff_2 (.D(d_ff_1_q), .C(TraceClock), .Q(d_ff_2_q));  // open: nQ
  PullDown #(.Bits(24)) pulldown_1 (.out(DBUS));
  and and_3 (and_3_out, _74ls175_1_q1, _74ls175_2_nq1);
  and and_4 (and_4_out, _74ls175_1_q2, _74ls175_2_nq2);
  and and_5 (and_5_out, _74ls175_1_q3, _74ls175_2_nq3);
  and and_6 (and_6_out, _74ls175_1_q4, _74ls175_2_nq4);
  D_FF d_ff_3 (.D(d_ff_2_q), .C(TraceClock), .nQ(POR));  // open: Q
  or or_5 (or_5_out, and_4_out, and_5_out);
  not not_2 (not_2_out, and_6_out);
  nor nor_1 (nResetP, POR, and_3_out);
  Half7474 half7474_1 (
    .nSD(1'b1), .D(half7474_1_nq), .CP(or_5_out), .nRD(nResetP), .Q(half7474_1_q), .nQ(half7474_1_nq));
  // Probe on not_2_out
  Half7474 half7474_2 (.nSD(not_2_out), .D(1'b0), .CP(MopEnd), .nRD(nResetP), .Q(half7474_2_q));  // open: nQ
  // Probe on nResetP
  LED led_1 (.in(half7474_2_q));
  not not_3 (nCK, XTAL);
  LED led_2 (.in(nResetP));
  Button M (.out(M_out));
  LED led_3 (.in(half7474_1_q));
  // Probe on half7474_1_q
  or or_6 (or_6_out, half7474_1_q, half7474_2_q);
  // Probe on half7474_2_q
  PullDown pulldown_2 (.out(half7474_2_q));
  Delay #(.delayTime(20)) delay_1 (.in(TS5), .out(delay_1_out));
  Counter #(.Bits(20)) counter_1 (.en(1'b1), .C(TS0), .clr(clk), .out(counter_1_out));  // open: ovf
  not not_4 (not_4_out, PCbit0);
  Half7474 half7474_3 (.nSD(1'b1), .D(M_out), .CP(nCK), .nRD(nResetP), .Q(half7474_3_q));  // open: nQ
  Half7474 half7474_4 (.nSD(1'b1), .D(or_6_out), .CP(nCK), .nRD(nResetP), .Q(RUN), .nQ(half7474_4_nq));
  and and_7 (and_7_out, PCneg, not_4_out);
  and and_8 (and_8_out, ~DBUS[0], DBUS[1], DBUS[2], DBUS[23], delay_1_out);  // And
  LED u_RUN (.in(RUN));
  // Probe on half7474_4_nq
  D_FF #(.Bits(20)) d_ff_4 (.D(counter_1_out), .C(clk), .Q(d_ff_4_q));  // open: nQ
  Button I (.out(INTREQ));
  // Probe on and_7_out
  // Not not_5 has open pins: in=and_7_out, out=open
  // Probe on and_8_out
  nor nor_2 (nor_2_out, half7474_4_nq, nCK);
  BarrelShifter #(.Bits(20)) barrelshifter_1 (.in(d_ff_4_q), .shift(5'b00011), .out(barrelshifter_1_out));
  // Probe on barrelshifter_1_out
  // Probe on MopEnd
  PullUp pullup_1 (.out(pullup_1_out));
  not not_6 (not_6_out, nResetP);
  or or_7 (Tick, and_3_out, half7474_3_q, nor_2_out);
  LED led_4 (.in(TS0));
  LED led_5 (.in(TS1));
  LED led_6 (.in(TS2));
  LED led_7 (.in(TS3));
  LED led_8 (.in(TS4));
  LED led_9 (.in(TS5));
  LED led_10 (.in(MopEnd));
  // Probe on SPY_PC
  // Probe on ABUS
  // Probe on DBUS
  // Probe on subleq24_gpio_1_port2out
  or or_8 (or_8_out, not_6_out, _74ls4017_1_q7);
  D_FF #(.Bits(24)) d_ff_5 (.D(DBUS), .C(MAR_CK), .Q(d_ff_5_q));  // open: nQ
  assign not_7_out = ~SPY_sub;  // Not not_7, 24 bits wide
  assign not_8_out = ~SPY_aval;  // Not not_8, 24 bits wide
  PullUp #(.Bits(24)) pullup_2 (.out(SPY_aval));
  PullDown #(.Bits(24)) pulldown_3 (.out(SPY_bval));
  not not_9 (not_9_out, MopEnd);
  Half7474 half7474_5 (.nSD(1'b1), .D(1'b1), .CP(INTREQ), .nRD(nResetP), .Q(half7474_5_q));  // open: nQ
  _74LS4017 _74ls4017_1 (
    .nCE(not_10_out), .CLK(Tick), .MR(or_8_out), .Q0(TS0), .Q1(TS1), .Q2(TS2), .Q3(TS3), .Q4(TS4), .Q5(TS5),
    .Q6(MopEnd), .Q7(_74ls4017_1_q7));  // open: Q8, Q9, nQ5_9
  not not_10 (not_10_out, pullup_1_out);
  // Probe MAR on d_ff_5_q
  // Probe PC on SPY_PC
  // Probe SUBT on SPY_sub
  // Probe ~SUBT on not_7_out
  // Probe ~AVAL on not_8_out
  // Probe BVAL on SPY_bval
  _74LS245 _74ls245_1 (
    .DIR(1'b1), .A1(1'b0), .A2(1'b1), .A3(1'b1), .A4(1'b0), .A5(1'b0), .A6(1'b0), .A7(1'b0), .A8(1'b0),
    .nOE(undriven_2), .B1(DBUS[0]), .B2(DBUS[1]), .B3(DBUS[2]), .B4(DBUS[3]), .B5(DBUS[4]), .B6(DBUS[5]),
    .B7(DBUS[6]), .B8(DBUS[7]));
  _74LS245 _74ls245_2 (
    .DIR(1'b1), .A1(1'b0), .A2(1'b0), .A3(1'b0), .A4(1'b0), .A5(1'b0), .A6(1'b0), .A7(1'b0), .A8(1'b0),
    .nOE(undriven_2), .B1(DBUS[8]), .B2(DBUS[9]), .B3(DBUS[10]), .B4(DBUS[11]), .B5(DBUS[12]), .B6(DBUS[13]),
    .B7(DBUS[14]), .B8(DBUS[15]));
  _74LS245 _74ls245_3 (
    .DIR(1'b1), .A1(1'b0), .A2(1'b0), .A3(1'b0), .A4(1'b0), .A5(1'b0), .A6(1'b0), .A7(1'b0), .A8(1'b0),
    .nOE(undriven_2), .B1(DBUS[16]), .B2(DBUS[17]), .B3(DBUS[18]), .B4(DBUS[19]), .B5(DBUS[20]),
    .B6(DBUS[21]), .B7(DBUS[22]), .B8(DBUS[23]));
  Half7474 half7474_6 (.nSD(1'b1), .D(half7474_5_q), .CP(not_9_out), .nRD(nResetP));  // open: Q, nQ
  LED led_11 (.in(TS0));
  not not_11 (not_11_out, TS0);
  nand nand_1 (nand_1_out, TS3, BisNeg);
  nand nand_2 (nand_2_out, TS1, AisNeg);
  LED led_12 (.in(TS1));
  LED led_13 (.in(TS2));
  Half7474 half7474_7 (.nSD(nand_1_out), .D(1'b0), .CP(nResetP), .nRD(not_11_out), .Q(IOwrite), .nQ(nIOwrite));
  Half7474 half7474_8 (.nSD(nand_2_out), .D(1'b0), .CP(nResetP), .nRD(not_11_out), .Q(IOread), .nQ(nIOread));
  LED led_14 (.in(TS3));
  LED led_15 (.in(TS4));
  PullUp pullup_3 (.out(pullup_3_out));
  // Probe on IOwrite
  // Probe on IOread
  LED led_16 (.in(TS5));
  _74LS574 _74ls574_1 (
    .nOC(pullup_3_out), .CLK(undriven), .D0(ABUS[0]), .D1(ABUS[1]), .D2(ABUS[2]), .D3(ABUS[3]), .D4(ABUS[4]),
    .D5(ABUS[5]), .D6(ABUS[6]), .D7(ABUS[7]), .Q0(DBUS[0]), .Q1(DBUS[1]), .Q2(DBUS[2]), .Q3(DBUS[3]),
    .Q4(DBUS[4]), .Q5(DBUS[5]), .Q6(DBUS[6]), .Q7(DBUS[7]), .SPY(_74ls574_1_spy));
  _74LS574 _74ls574_2 (
    .nOC(pullup_3_out), .CLK(undriven), .D0(ABUS[8]), .D1(ABUS[9]), .D2(ABUS[10]), .D3(ABUS[11]),
    .D4(ABUS[12]), .D5(ABUS[13]), .D6(ABUS[14]), .D7(ABUS[15]), .Q0(DBUS[8]), .Q1(DBUS[9]), .Q2(DBUS[10]),
    .Q3(DBUS[11]), .Q4(DBUS[12]), .Q5(DBUS[13]), .Q6(DBUS[14]), .Q7(DBUS[15]), .SPY(_74ls574_2_spy));
  _74LS574 _74ls574_3 (
    .nOC(pullup_3_out), .CLK(undriven), .D0(ABUS[16]), .D1(ABUS[17]), .D2(ABUS[18]), .D3(ABUS[19]),
    .D4(ABUS[20]), .D5(ABUS[21]), .D6(ABUS[22]), .D7(ABUS[23]), .Q0(DBUS[16]), .Q1(DBUS[17]), .Q2(DBUS[18]),
    .Q3(DBUS[19]), .Q4(DBUS[20]), .Q5(DBUS[21]), .Q6(DBUS[22]), .Q7(DBUS[23]), .SPY(_74ls574_3_spy));
  LED led_17 (.in(MopEnd));
  nand nand_3 (nand_3_out, TS4, IOwrite);
  nand nand_4 (nIOreadP, TS3, IOread);
  _74LS125 _74ls125_1 (
    .A4(1'b0), .nG1(nBusRq), .nG2(nBusRq), .nG3(nBusRq), .nG4(nBusRq), .Y1(nPC_E), .Y2(nPC_LD), .Y3(PC_CK),
    .Y4(_74ls125_1_y4));  // open: A1, A2, A3
  not not_12 (not_12_out, nand_3_out);
  not not_13 (nIOwriteP, not_12_out);
  and and_9 (and_9_out, TS3, nIOread, 1'b1);
  // Probe on {_74ls574_3_spy, _74ls574_2_spy, _74ls574_1_spy}
  not not_14 (not_14_out, nBusRq);
  or or_9 (or_9_out, TS0, TS1, TS2);
  or or_10 (seqPCck, TS1, TS3, MopEnd);
  or or_11 (or_11_out, TS1, TS3, 1'b0);
  or or_12 (or_12_out, TS1, TS3, TS4);
  and and_10 (and_10_out, TS4, nIOwrite, 1'b1);
  and and_11 (and_11_out, TS5, nIOwrite, isLEQ);
  or or_13 (or_13_out, TS0, TS2, TS5);
  or or_14 (or_14_out, or_9_out, TS5, and_9_out);
  _74LS541 _74ls541_1 (
    .nOE1(not_14_out), .nOE2(not_14_out), ._0D(TS1), ._1D(TS3), ._2D(TS2), ._3D(TS4), ._4D(seqPCck),
    ._5D(or_11_out), ._6D(1'b0), ._7D(1'b0), ._0O(A_CK), ._1O(B_CK), ._2O(Aval_CK), ._3O(Bval_CK),
    ._4O(PC_CK), ._5O(MAR_CK), ._6O(_74ls541_1__6o), ._7O(_74ls541_1__7o));
  _74LS540 _74ls540_1 (
    .nOE1(not_14_out), .nOE2(not_14_out), ._0D(TS4), ._1D(or_12_out), ._2D(and_10_out), ._3D(and_11_out),
    ._4D(or_13_out), ._5D(or_14_out), ._6D(1'b0), ._7D(1'b0), .n0O(nResult_E), .n1O(nMAR_E), .n2O(nWR),
    .n3O(nPC_LD), .n4O(nPC_E), .n5O(nRD), .n6O(_74ls540_1_n6o), .n7O(_74ls540_1_n7o));
  PullDown pulldown_4 (.out(A_CK));
  PullDown pulldown_5 (.out(B_CK));
  PullUp pullup_4 (.out(nResult_E));
  PullUp pullup_5 (.out(nMAR_E));
  PullDown pulldown_6 (.out(Aval_CK));
  PullDown pulldown_7 (.out(Bval_CK));
  PullDown pulldown_8 (.out(PC_CK));
  PullDown pulldown_9 (.out(MAR_CK));
  PullUp pullup_6 (.out(nWR));
  PullUp pullup_7 (.out(nPC_LD));
  PullUp pullup_8 (.out(nPC_E));
  PullUp pullup_9 (.out(nRD));
  PullDown pulldown_10 (.out(_74ls541_1__6o));
  PullDown pulldown_11 (.out(_74ls541_1__7o));
  PullUp pullup_10 (.out(_74ls540_1_n6o));
  PullUp pullup_11 (.out(_74ls540_1_n7o));
  // Probe on SPY_PC
  // Probe on ABUS
  // Probe on DBUS
  LED led_18 (.in(isLEQ));
  LED led_19 (.in(TS0));
  LED led_20 (.in(TS1));
  LED led_21 (.in(TS2));
  LED led_22 (.in(TS3));
  LED led_23 (.in(TS4));
  LED led_24 (.in(TS5));
  LED led_25 (.in(MopEnd));

  // Other names for the same wires on the sheet: CK = XTAL; TS6 = MopEnd

  // Notes on the sheet:
  //   XTAL: Hz: 50000
  //   TraceClock: Hz: 10
  //   clk: Hz: 4
  //   BAUDCLK: Hz: 153600
  //   RUN/HALT
  //   CONTROL/SEQUENCER
  //   STEP
  //   RESET-F
  //   RESET-R
  //   diode
  //   steering
  //   MEMORY
  //   microSTEP
  //   U20
  //   U21
  //   INTERUPT
  //   INTERRUPT
  //   -----------------------
  //   Save current PC to holding register
  //   Set PC to 6
  //   RETURN FROM INTERRUPT
  //   (initiated by goto -2)
  //   -----------------------
  //   SET PC to holding register
  //   MICROCODE
  //   if(a < 0) mem[b] += (int)getchar(); /* input */
  //           else if(b < 0) printf("%c", (char)mem[a]); /* output */
  //   stty -icanon -echo && nc localhost 23
endmodule
