// Digital circuit Uart_Telnet_GW.dig as structural Verilog
module Uart_Telnet_GW (
  input  RX,
  input  CLK,
  output TX
);

  wire and_1_out, d_ff_1_q, d_ff_2_q, d_ff_3_q, d_ff_4_q, d_ff_5_q, d_ff_6_q, d_ff_7_nq, delay_1_out,
       delay_2_out, delay_3_out, not_1_out, or_1_out, or_2_out, telnet_1_av, uartrx_1_rdy;
  wire [7:0] not_2_out, telnet_1_out, uartrx_1_nq;

  UartRx uartrx_1 (.RX(RX), .nACK(not_1_out), .nOE(1'b0), .CLK(CLK), .nQ(uartrx_1_nq), .RDY(uartrx_1_rdy));
  not not_1 (not_1_out, delay_1_out);
  D_FF d_ff_1 (.D(1'b1), .C(CLK), .Q(d_ff_1_q));  // open: nQ
  Delay #(.delayTime(20)) delay_1 (.in(uartrx_1_rdy), .out(delay_1_out));
  D_FF d_ff_2 (.D(d_ff_1_q), .C(CLK), .Q(d_ff_2_q));  // open: nQ
  assign not_2_out = ~uartrx_1_nq;  // Not not_2, 8 bits wide
  D_FF d_ff_3 (.D(d_ff_2_q), .C(CLK), .Q(d_ff_3_q));  // open: nQ
  Delay #(.delayTime(10)) delay_2 (.in(or_1_out), .out(delay_2_out));
  or or_1 (or_1_out, delay_3_out, uartrx_1_rdy);
  D_FF d_ff_4 (.D(d_ff_3_q), .C(CLK), .Q(d_ff_4_q));  // open: nQ
  PullDown pulldown_1 (.out(delay_2_out));
  PullDown pulldown_2 (.out(uartrx_1_rdy));
  and and_1 (and_1_out, d_ff_6_q, d_ff_7_nq);
  D_FF d_ff_5 (.D(d_ff_4_q), .C(CLK), .Q(d_ff_5_q));  // open: nQ
  Telnet #(.telnetEscape("false")) telnet_1 (
    .in(not_2_out), .C(delay_2_out), .wr(uartrx_1_rdy), .rd(telnet_1_av), .out(telnet_1_out), .av(telnet_1_av));
  PullDown pulldown_3 (.out(telnet_1_av));
  Delay #(.delayTime(5)) delay_3 (.in(telnet_1_av), .out(delay_3_out));
  // Probe on delay_3_out
  D_FF d_ff_6 (.D(d_ff_5_q), .C(CLK), .Q(d_ff_6_q));  // open: nQ
  // Probe on telnet_1_out
  PullDown #(.Bits(8)) pulldown_4 (.out(telnet_1_out));
  or or_2 (or_2_out, delay_3_out, and_1_out);
  D_FF d_ff_7 (.D(d_ff_6_q), .C(CLK), .nQ(d_ff_7_nq));  // open: Q
  UartTx uarttx_1 (.nD(telnet_1_out), .STB(or_2_out), .CLK(CLK), .TX(TX));  // open: BSY
  // Probe on TX

  // Notes on the sheet:
  //   CLK: Hz: 10
  //   SERIAL -> TELNET GATEWAY
  //   ONLY FOR TESTING IN SIMULATION
endmodule
